// Logisim project Little Computer.circ as structural Verilog: 3 circuits, main circuit main
module main (
);

  wire clock_1_out, control_unit_1_acc_data_selector, control_unit_1_acc_enable,
       control_unit_1_alu_a_selector, control_unit_1_ir_enable, control_unit_1_mem_address_selector,
       control_unit_1_mem_store, control_unit_1_pc_data_selector, control_unit_1_pc_enable,
       control_unit_1_successor_enable;
  wire [1:0] control_unit_1_alu_b_selector, control_unit_1_alu_op;
  wire [7:0] bit_extender_1_out, control_unit_1_operand, multiplexer_1_out, multiplexer_3_out, PC_q,
       successor_q;
  wire [11:0] ACC_q, arithmetic_logic_unit_1_c, bit_extender_2_out, IR_q, multiplexer_2_out,
       multiplexer_4_out, multiplexer_5_out, ram_1_data;

  Control_Unit control_unit_1 (
    .clock(clock_1_out), .ALU_C(arithmetic_logic_unit_1_c), .IR(IR_q),
    .successor_enable(control_unit_1_successor_enable), .PC_data_selector(control_unit_1_pc_data_selector),
    .PC_enable(control_unit_1_pc_enable), .IR_enable(control_unit_1_ir_enable),
    .ACC_data_selector(control_unit_1_acc_data_selector), .ACC_enable(control_unit_1_acc_enable),
    .ALU_A_selector(control_unit_1_alu_a_selector), .ALU_B_selector(control_unit_1_alu_b_selector),
    .ALU_op(control_unit_1_alu_op), .Mem_address_selector(control_unit_1_mem_address_selector),
    .Mem_store(control_unit_1_mem_store), .operand(control_unit_1_operand));
  Bit_Extender #(.in_width(12), .out_width(8)) bit_extender_1 (
    .in(arithmetic_logic_unit_1_c), .out(bit_extender_1_out));
  Multiplexer #(.width(8), .enable("false")) multiplexer_1 (
    .in0(successor_q), .in1(control_unit_1_operand), .out(multiplexer_1_out),
    .sel(control_unit_1_pc_data_selector));
  Multiplexer #(.width(12), .enable("false")) multiplexer_2 (
    .in0(arithmetic_logic_unit_1_c), .in1(ram_1_data), .out(multiplexer_2_out),
    .sel(control_unit_1_acc_data_selector));
  Multiplexer #(.width(8), .enable("false")) multiplexer_3 (
    .in0(PC_q), .in1(control_unit_1_operand), .out(multiplexer_3_out),
    .sel(control_unit_1_mem_address_selector));
  Register successor (
    .D(bit_extender_1_out), .en(control_unit_1_successor_enable), .Q(successor_q), .clk(clock_1_out));  // open: clr
  Register PC (.D(multiplexer_1_out), .en(control_unit_1_pc_enable), .Q(PC_q), .clk(clock_1_out));  // open: clr
  Register #(.width(12)) IR (.D(ram_1_data), .en(control_unit_1_ir_enable), .Q(IR_q), .clk(clock_1_out));  // open: clr
  Register #(.width(12)) ACC (
    .D(multiplexer_2_out), .en(control_unit_1_acc_enable), .Q(ACC_q), .clk(clock_1_out));  // open: clr
  Clock clock_1 (.out(clock_1_out));
  assign bit_extender_2_out = {{4{1'b0}}, PC_q};  // Bit_Extender bit_extender_2
  Multiplexer #(.width(12), .enable("false")) multiplexer_4 (
    .in0(bit_extender_2_out), .in1(ACC_q), .out(multiplexer_4_out), .sel(control_unit_1_alu_a_selector));
  RAM #(.dataWidth(12), .bus("separate")) ram_1 (
    .addr(multiplexer_3_out), .din(ACC_q), .data(ram_1_data), .str(control_unit_1_mem_store),
    .clk(clock_1_out));  // open: sel, ld, clr
  Multiplexer #(.select(2), .width(12), .enable("false")) multiplexer_5 (
    .in0({12{1'b0}}), .in1(12'h1), .in2(ram_1_data), .out(multiplexer_5_out),
    .sel(control_unit_1_alu_b_selector));  // open: in3
  Arithmetic_Logic_Unit arithmetic_logic_unit_1 (
    .A(multiplexer_4_out), .B(multiplexer_5_out), .op(control_unit_1_alu_op), .C(arithmetic_logic_unit_1_c));
endmodule

// ALU
module Arithmetic_Logic_Unit (
  input  [11:0] A,
  input  [11:0] B,
  input  [1:0] op,
  output [11:0] C
);

  wire comparator_1_eq, comparator_1_lt, multiplexer_2_out, not_1_out;
  wire [11:0] adder_1_out, bit_extender_1_out, multiplexer_1_out, subtractor_1_out;

  Adder #(.width(12)) adder_1 (.a(A), .b(B), .out(adder_1_out));  // open: cin, cout
  Subtractor #(.width(12)) subtractor_1 (.a(A), .b(B), .out(subtractor_1_out));  // open: bin, bout
  Comparator #(.width(12)) comparator_1 (.a(A), .b(B), .eq(comparator_1_eq), .lt(comparator_1_lt));  // open: gt
  not not_1 (not_1_out, comparator_1_lt);
  Multiplexer #(.width(12), .enable("false")) multiplexer_1 (
    .in0(adder_1_out), .in1(subtractor_1_out), .out(multiplexer_1_out), .sel(op[0]));
  Multiplexer #(.enable("false")) multiplexer_2 (
    .in0(comparator_1_eq), .in1(not_1_out), .out(multiplexer_2_out), .sel(op[0]));
  assign bit_extender_1_out = {{11{1'b0}}, multiplexer_2_out};  // Bit_Extender bit_extender_1
  Multiplexer #(.width(12), .enable("false")) multiplexer_3 (
    .in0(multiplexer_1_out), .in1(bit_extender_1_out), .out(C), .sel(op[1]));

  // Notes on the sheet:
  //   00 A+B, 01 A-B, 10 A==B, 11 A>=B
endmodule

// CU
module Control_Unit (
  input  clock,
  input  [11:0] ALU_C,
  input  [11:0] IR,
  output successor_enable,
  output PC_data_selector,
  output PC_enable,
  output IR_enable,
  output ACC_data_selector,
  output ACC_enable,
  output ALU_A_selector,
  output [1:0] ALU_B_selector,
  output [1:0] ALU_op,
  output Mem_address_selector,
  output Mem_store,
  output [7:0] operand
);

  wire and_1_out, bit_extender_1_out, decoder_1_out0, decoder_1_out1, decoder_1_out2, decoder_1_out3,
       decoder_1_out6, decoder_1_out7, decoder_1_out8, or_1_out, or_3_out, or_4_out, or_5_out;

  Decoder #(.select(4), .enable("false")) decoder_1 (
    .out0(decoder_1_out0), .out1(decoder_1_out1), .out2(decoder_1_out2), .out3(decoder_1_out3),
    .out5(ACC_data_selector), .out6(decoder_1_out6), .out7(decoder_1_out7), .out8(decoder_1_out8),
    .sel(IR[11:8]));  // open: out4, out9, out10, out11, out12, out13, out14, out15
  Counter #(.width(1), .max('h1)) phase (.Q(ALU_A_selector), .clk(clock));  // open: load, D, count, carry, clr
  Bit_Extender #(.in_width(12), .out_width(1)) bit_extender_1 (.in(ALU_C), .out(bit_extender_1_out));
  or or_1 (or_1_out, decoder_1_out7, decoder_1_out8);
  or or_2 (PC_data_selector, decoder_1_out6, and_1_out);
  and and_1 (and_1_out, bit_extender_1_out, or_1_out);
  or or_3 (or_3_out, ACC_data_selector, decoder_1_out1, decoder_1_out2);
  not not_1 (successor_enable, ALU_A_selector);
  and and_2 (PC_enable, ALU_A_selector, ~decoder_1_out0);  // AND_Gate
  not not_2 (IR_enable, ALU_A_selector);
  and and_3 (ACC_enable, ALU_A_selector, or_3_out);
  not not_3 (ALU_B_selector[0], ALU_A_selector);
  and and_4 (ALU_B_selector[1], ~or_1_out, ALU_A_selector);  // AND_Gate
  and and_5 (ALU_op[0], ALU_A_selector, or_4_out);
  or or_4 (or_4_out, decoder_1_out2, decoder_1_out8);
  and and_6 (ALU_op[1], ALU_A_selector, or_5_out);
  or or_5 (or_5_out, decoder_1_out7, decoder_1_out8);
  and and_7 (Mem_store, ALU_A_selector, decoder_1_out3);

  assign Mem_address_selector = ALU_A_selector;
  assign operand = IR[7:0];

  // Notes on the sheet:
  //   0 fetch, 1 execute
endmodule
